# Fritzing sketch Sketch 2 (saved by Fritzing 0.9.3b)
breadboards: 1

parts:
  元件1 = Arduino Uno (Rev3)
  R1 = Resistor [tolerance=±5% resistance=220 package=THT]
  LED1 = LED - 5mm [color="Red (633nm)" package="5 mm [THT]"]
  S1 = Pushbutton [package="[THT]"]
  R2 = Resistor [tolerance=±5% resistance=220 package=THT]

nets:
  N1: 元件1.D8, S1.Pin_1, S1.Pin_2, R2.Pin_0
  N2: 元件1.D2, R1.Pin_1
  N3: 元件1.5V, S1.Pin_3, S1.Pin_4
  N4: 元件1.GND, LED1.cathode, R2.Pin_1
  N5: R1.Pin_0, LED1.anode
